# Fritzing sketch circuito (saved by Fritzing 0.9.2b)
breadboards: 1

parts:
  LCD1 = LCD screen
  R1 = Rotary Potentiometer (Small) [maximum_resistance=100kΩ package=THT]
  T1 = TMP36 Temperature Sensor [package="TO92 [THT]"]
  R2 = Resistor [tolerance=±5% resistance=220 package=THT]
  Parte3 = Arduino Yun
  DHT1 = DHT11 Humitidy and Temperature Sensor

nets:
  GND: LCD1.VSS, LCD1.R/W, LCD1.LED-, R1.leg2, T1.GND, Parte3.GND, DHT1.GND
  VDD: LCD1.VDD, R1.leg1, T1.+Vs, R2.Pin_0, Parte3.5V, DHT1.VDD
  N1: LCD1.V0, R1.wiper
  N2: LCD1.RS, Parte3.D8
  N3: LCD1.E, Parte3.D9_PWM
  N4: LCD1.DB4, Parte3.D6_PWM
  N5: LCD1.DB5, Parte3.D5_PWM
  N6: LCD1.DB6, Parte3.D3_PWM
  N7: LCD1.DB7, Parte3.D2
  N8: LCD1.LED+, R2.Pin_1
  N9: T1.Vout, Parte3.A0
  N10: Parte3.D7, DHT1.DATA

custom parts:
  DHT11 Humitidy and Temperature Sensor: DHT11 Humidity and Temperature Sensor
